# Fritzing sketch full wiring diagram (saved by Fritzing 0.9.4)
breadboards: 6
perfboards: 1

parts:
  IC1 = IC, DIP package, 16 pins [chip_label=CD4051B]
  Part1 = Arduino Uno (Rev3) - ICSP
  U1 = POT [package=pot_mammoth]
  U2 = POT [package=pot_mammoth]
  U3 = POT [package=pot_mammoth]
  U4 = POT [package=pot_mammoth]
  U5 = POT [package=pot_mammoth]
  U6 = POT [package=pot_mammoth]
  U7 = POT [package=pot_mammoth]
  U8 = POT [package=pot_mammoth]
  IC2 = IC, DIP package, 16 pins [chip_label=CD4051B]
  U9 = POT [package=pot_mammoth]
  U10 = POT [package=pot_mammoth]
  U11 = POT [package=pot_mammoth]
  U12 = POT [package=pot_mammoth]
  U13 = POT [package=pot_mammoth]
  U14 = POT [package=pot_mammoth]
  U15 = POT [package=pot_mammoth]
  U16 = POT [package=pot_mammoth]
  RE2 = Rotary Encoder [package=THT]  # not connected
  S1 = Square Pushbutton
  LED1 = smd LED [color="Red (633nm)" package="0805 [SMD]"]
  LED2 = smd LED [color="Red (633nm)" package="0805 [SMD]"]
  LED3 = smd LED [color="Red (633nm)" package="0805 [SMD]"]
  LED4 = smd LED [color="Red (633nm)" package="0805 [SMD]"]
  LED5 = smd LED [color="Red (633nm)" package="0805 [SMD]"]
  LED6 = smd LED [color="Red (633nm)" package="0805 [SMD]"]
  LED7 = smd LED [color="Red (633nm)" package="0805 [SMD]"]
  LED8 = smd LED [color="Red (633nm)" package="0805 [SMD]"]
  LED9 = smd LED [color="Red (633nm)" package="0805 [SMD]"]
  LED10 = smd LED [color="Red (633nm)" package="0805 [SMD]"]
  LED11 = smd LED [color="Red (633nm)" package="0805 [SMD]"]
  LED12 = smd LED [color="Red (633nm)" package="0805 [SMD]"]
  LED13 = smd LED [color="Red (633nm)" package="0805 [SMD]"]
  LED14 = smd LED [color="Red (633nm)" package="0805 [SMD]"]
  LED15 = smd LED [color="Red (633nm)" package="0805 [SMD]"]
  LED16 = smd LED [color="Red (633nm)" package="0805 [SMD]"]
  R1 = Resistor [tolerance=±5% resistance=220 package="1206 [SMD]"]
  IC3 = IC, DIP package, 16 pins [chip_label=CD4051B]
  IC4 = IC, DIP package, 16 pins [chip_label=CD4051B]
  R2 = Resistor [tolerance=±5% resistance=220 package="1206 [SMD]"]
  R3 = Resistor [tolerance=±5% resistance=220 package="1206 [SMD]"]
  R4 = Resistor [tolerance=±5% resistance=220 package="1206 [SMD]"]
  R5 = Resistor [tolerance=±5% resistance=220 package="1206 [SMD]"]
  R6 = Resistor [tolerance=±5% resistance=220 package="1206 [SMD]"]
  R7 = Resistor [tolerance=±5% resistance=220 package="1206 [SMD]"]
  R8 = Resistor [tolerance=±5% resistance=220 package="1206 [SMD]"]
  R9 = Resistor [tolerance=±5% resistance=220 package="1206 [SMD]"]
  R10 = Resistor [tolerance=±5% resistance=220 package="1206 [SMD]"]
  R11 = Resistor [tolerance=±5% resistance=220 package="1206 [SMD]"]
  R12 = Resistor [tolerance=±5% resistance=220 package="1206 [SMD]"]
  R13 = Resistor [tolerance=±5% resistance=220 package="1206 [SMD]"]
  R14 = Resistor [tolerance=±5% resistance=220 package="1206 [SMD]"]
  R15 = Resistor [tolerance=±5% resistance=220 package="1206 [SMD]"]
  R16 = Resistor [tolerance=±5% resistance=220 package="1206 [SMD]"]
  R17 = Resistor [tolerance=±5% resistance=220 package="1206 [SMD]"]

nets:
  N1: IC1.pin1, U5.A
  N2: IC1.pin2, U7.A
  N3: IC1.pin3, Part1.A0
  N4: IC1.pin4, U8.A
  N5: IC1.pin5, U6.A
  N6: IC1.pin6, Part1.D7, IC2.pin6, IC3.pin6, IC4.pin6
  N7: IC1.pin8, Part1.GND, U1.S, U2.S, U3.S, U4.S, U5.S, U6.S, U7.S, U8.S, IC2.pin8, U9.S, U10.S, U11.S, U12.S, U13.S, U14.S, U15.S, U16.S, LED1.cathode, LED2.cathode, LED3.cathode, LED4.cathode, LED5.cathode, LED9.cathode, LED14.cathode, LED15.cathode, LED16.cathode, R1.Pin_0, IC3.pin8, IC4.pin8
  N8: IC1.pin9, Part1.D10_PWM/SS, IC2.pin9, IC3.pin11, IC4.pin11
  N9: IC1.pin10, Part1.D9_PWM, IC2.pin10, IC3.pin10, IC4.pin10
  N10: IC1.pin11, Part1.D8, IC2.pin11, IC3.pin9, IC4.pin9
  N11: IC1.pin12, U4.A
  N12: IC1.pin13, U1.A
  N13: IC1.pin14, U2.A
  N14: IC1.pin15, U3.A
  N15: IC1.pin16, Part1.5V, U1.E, U2.E, U3.E, U4.E, U5.E, U6.E, U7.E, U8.E, IC2.pin16, U9.E, U10.E, U11.E, U12.E, U13.E, U14.E, U15.E, U16.E, S1.leg1, IC3.pin16, IC4.pin16
  N16: Part1.A1, IC2.pin3
  N17: Part1.A2, IC3.pin3
  N18: Part1.A3, IC4.pin3
  N19: Part1.A4/SDA, S1.leg0, R1.Pin_1
  N20: IC2.pin1, U13.A
  N21: IC2.pin2, U15.A
  N22: IC2.pin4, U16.A
  N23: IC2.pin5, U14.A
  N24: IC2.pin12, U12.A
  N25: IC2.pin13, U9.A
  N26: IC2.pin14, U10.A
  N27: IC2.pin15, U11.A
  N28: LED1.anode, R9.Pin_0
  N29: LED2.anode, R8.Pin_0
  N30: LED3.anode, R7.Pin_0
  N31: LED4.anode, R6.Pin_0
  N32: LED5.anode, R5.Pin_0
  N33: LED6.cathode, LED7.cathode, LED8.cathode
  N34: LED6.anode, R4.Pin_0
  N35: LED7.anode, R2.Pin_0
  N36: LED8.anode, R3.Pin_0
  N37: LED9.anode, R17.Pin_0
  N38: LED10.cathode, LED11.cathode, LED12.cathode, LED13.cathode
  N39: LED10.anode, R10.Pin_0
  N40: LED11.anode, R11.Pin_0
  N41: LED12.anode, R12.Pin_0
  N42: LED13.anode, R13.Pin_0
  N43: LED14.anode, R14.Pin_0
  N44: LED15.anode, R15.Pin_0
  N45: LED16.anode, R16.Pin_0
  N46: IC3.pin1, R5.Pin_1
  N47: IC3.pin2, R2.Pin_1
  N48: IC3.pin4, R3.Pin_1
  N49: IC3.pin5, R4.Pin_1
  N50: IC3.pin12, R14.Pin_1
  N51: IC3.pin13, R9.Pin_1
  N52: IC3.pin14, R8.Pin_1
  N53: IC3.pin15, R7.Pin_1
  N54: IC4.pin1, R13.Pin_1
  N55: IC4.pin2, R11.Pin_1
  N56: IC4.pin4, R10.Pin_1
  N57: IC4.pin5, R12.Pin_1
  N58: IC4.pin12, R6.Pin_1
  N59: IC4.pin13, R17.Pin_1
  N60: IC4.pin14, R16.Pin_1
  N61: IC4.pin15, R15.Pin_1
